# Fritzing sketch keypad (saved by Fritzing 0.9.2b)
circuit board: 4.8cm x 4.55cm
stripboards: 1

parts:
  S1 = Pushbutton [package="[THT]"]
  S2 = Pushbutton [package="[THT]"]
  S3 = Pushbutton [package="[THT]"]
  S4 = Pushbutton [package="[THT]"]
  R1 = Resistor [tolerance=±5% resistance=10k package=THT]
  R2 = Resistor [tolerance=±5% resistance=10k package=THT]
  R3 = Resistor [tolerance=±5% resistance=10k package=THT]
  R5 = Resistor [tolerance=±5% resistance=10k package=THT]
  R6 = Resistor [tolerance=±5% resistance=10k package=THT]
  R7 = Resistor [tolerance=±5% resistance=1M package=THT]
  J1 = molex pin header, 3 pins [form=molex]
  R4 = Resistor [tolerance=±5% resistance=10k package=THT]
  S5 = Pushbutton [package="[THT]"]

nets:
  N1: S1.Pin_1, S1.Pin_2, R1.Pin_1, R2.Pin_0
  A0: S1.Pin_3, S1.Pin_4, S2.Pin_3, S2.Pin_4, S3.Pin_3, S3.Pin_4, S4.Pin_1, S4.Pin_2, R7.Pin_0, J1.pin2, S5.Pin_3, S5.Pin_4
  N2: S2.Pin_1, S2.Pin_2, R2.Pin_1, R3.Pin_1
  N3: S3.Pin_1, S3.Pin_2, R3.Pin_0, R4.Pin_1
  N4: S4.Pin_3, S4.Pin_4, R5.Pin_0, R4.Pin_0
  5V: R1.Pin_0, J1.pin1
  N5: R5.Pin_1, R6.Pin_1, S5.Pin_1, S5.Pin_2
  GND: R6.Pin_0, R7.Pin_1, J1.pin3

notes:
  Escornabot, Analog keypad for Escornabot «Kanoi» (v0.3) with only 5 buttons, 1.3
  Escornabot
  5V
  SIG
  GND
  escornawiki.org
  2015 (CC BY-SA) Xoan Sampaiño
  R1-R6: 10 KOhm
  R7:  1 MOhm
  Keypad v1.3
